# Fritzing sketch door-lock (saved by Fritzing 0.9.4)
breadboards: 1

parts:
  U1 = ESP32-38PinWide [part_number=ESP32-38PinWide]
  J1 = Basic Servo
  BAT1 = Battery Holders [package=lipo-1100mAh]

nets:
  GND: U1.GND, J1.gnd, BAT1.-
  N1: U1.GPIO18, J1.pulse
  N2: J1.vcc, BAT1.+

custom parts:
  ESP32-38PinWide: Generic 38-Pin ESP32 with wide format (only access to one side of pins on a breadboard) based on Stephen Lilley's HiLetgo ESP-WROOM-32 ESP32 ESP-32S Development Board.
